# Fritzing sketch Untitled Sketch (saved by Fritzing 0.9.6b)
breadboards: 1

parts:
  Componente1 = Arduino Uno (Rev3)
  U1 = ESP8266 ESP-01 Upgraded WiFi Module [part_number=ESP8266]
  LED1 = smd LED [color="Red (633nm)" package="0603 [SMD]"]
  S5 = Taiway 100-SP-X-T1 SPDT Miniature Toggle Switch [part_number=100-SP-X-T1-0-0-B1-M2 package=THT]
  S6 = Pushbutton [package="[SMD]"]

nets:
  GND: Componente1.GND, U1.RST/GPIO_16, U1.GND, S5.L1, S6.Pin_1, S6.Pin_2, S6.Pin_3, S6.Pin_4
  N1: Componente1.D0/RX, U1.RXD
  N2: Componente1.D1/TX, U1.TXD
  3V3: Componente1.3V3, U1.VCC, U1.CH_PD, LED1.anode
  N3: U1.GPIO_0, S5.L2
  N4: U1.GPIO_2, LED1.cathode

notes:
  conectar a tierra para programar el esp
  conectar a tierra para resetear el esp
  se debe remover el chip controlador del arduino

custom parts:
  ESP8266 ESP-01 Upgraded WiFi Module: Upgraded Version ESP-01,all Flash are upgraded to 1M byte.Also support Cloud service remote transmission.
